# Fritzing sketch dcdc_enable (saved by Fritzing 0.9.3b)
breadboards: 1

parts:
  Q1 = NPN-Transistor [part_number=9014 package="TO92 [THT]"]
  R1 = Resistor [tolerance=±5% resistance=10k package=THT]
  Q2 = Basic FET N-Channel [part_number=IRLM0030 package="DPak [SMD]"]
  R2 = Resistor [tolerance=±5% resistance=100k package=THT]
  R3 = Resistor [tolerance=±5% resistance=1k package=THT]
  R4 = Resistor [tolerance=±5% resistance=10k package=THT]
  R7 = Resistor [tolerance=±5% resistance=1k package=THT]
  D2 = Zener Diode [part_number=15v breakdown_voltage=3.6V package="300 mil [THT]"]
  R8 = Resistor [tolerance=±5% resistance=100k package=THT]
  Q4 = Basic FET N-Channel [part_number=IRLM0030 package="DPak [SMD]"]
  r9 = Resistor [tolerance=±5% resistance=15k package=THT]

nets:
  GND: Q1.E, R1.Pin_1, Q2.source, Q4.source, r9.Pin_1
  ENABLE: Q1.C, Q2.Gate
  N1: Q2.drain, R3.Pin_1
  20V: R2.Pin_0, R8.Pin_0
  STBY: R3.Pin_0, R7.Pin_0
  DCDC Enable: R4.Pin_1
  N2: R7.Pin_1, Q4.drain
  N3: D2.cathode, R8.Pin_1
  N4: D2.anode, Q4.Gate, r9.Pin_0

notes:
  Vin actually
  Vout actually
