# Fritzing sketch pw24 (saved by Fritzing 0.9.3b)
circuit board: 8.46667cm x 5.64444cm
breadboards: 1

parts:
  U1 = LM 358 Dual Op-Amp [package="DIP8 [THT]"]
  RShunt = Resistor [tolerance=±5% resistance=50m package=THT]
  U2 = LM 358 Dual Op-Amp [package="DIP8 [THT]"]
  U3 = LM 358 Dual Op-Amp [package="DIP8 [THT]"]
  C3 = Ceramic Capacitor [capacitance=100nF package="100 mil [THT, multilayer]"]
  R14 = Resistor [tolerance=±5% resistance=15k package="0603 [SMD]"]
  R15 = Resistor [tolerance=±5% resistance=1k package="0603 [SMD]"]
  R5 = Resistor [tolerance=±5% resistance=100k package="0603 [SMD]"]
  R4 = Resistor [tolerance=±5% resistance=1k package="0603 [SMD]"]
  R2 = Resistor [tolerance=±5% resistance=10k package="0603 [SMD]"]
  R3 = Resistor [tolerance=±5% resistance=1k package="0603 [SMD]"]
  R1 = Resistor [tolerance=±5% resistance=10k package="0603 [SMD]"]
  R6 = Resistor [tolerance=±5% resistance=100k package="0603 [SMD]"]
  R7 = Resistor [tolerance=±5% resistance=100k package="0603 [SMD]"]
  R8 = Resistor [tolerance=±5% resistance=100k package="0603 [SMD]"]
  R9 = Resistor [tolerance=±5% resistance=22k package="0603 [SMD]"]
  R17 = Resistor [tolerance=±5% resistance=0 part_number=!!120k!! package="0603 [SMD]"]
  R11 = Resistor [tolerance=±5% resistance=47k package="0603 [SMD]"]
  R10 = Resistor [tolerance=±5% resistance=22k package="0603 [SMD]"]
  U4 = LM 358 Dual Op-Amp [package="DIP8 [THT]"]
  R22 = Resistor [tolerance=±5% resistance=100 package="0603 [SMD]"]
  LED1 = LED - 5mm [color="Red (633nm)" package="5 mm [THT]"]
  D4 = Zener Diode [part_number=1N4732A breakdown_voltage=3.6V package="300 mil [THT]"]
  D3 = Zener Diode [part_number=1N4732A breakdown_voltage=3.6V package="300 mil [THT]"]
  D6 = Zener Diode [part_number=1N4732A breakdown_voltage=3.6V package="300 mil [THT]"]
  U5 = MCP4725 [package=SOT23-6]
  U7 = MCP4725 [package=SOT23-6]
  D8 = Zener Diode [part_number=1N4732A breakdown_voltage=3.6V package="300 mil [THT]"]
  D9 = Zener Diode [part_number=1N4732A breakdown_voltage=3.6V package="300 mil [THT]"]
  C8 = Electrolytic Capacitor [capacitance=40µF package="100 mil [THT, electrolytic]"]
  C9 = Electrolytic Capacitor [capacitance=40µF package="100 mil [THT, electrolytic]"]
  C10 = Ceramic Capacitor [capacitance=100nF package="100 mil [THT, multilayer]"]
  U9 = V_REG_LD1117VXX [package=78xxl]
  R23 = Resistor [tolerance=±5% resistance=10k package=THT]
  C12 = Electrolytic Capacitor [capacitance=330µF package="100 mil [THT, electrolytic]"]
  C13 = Electrolytic Capacitor [capacitance=330µF package="100 mil [THT, electrolytic]"]
  L1 = Inductor [inductance=330µH part_number=10mH package="400 mil [THT]"]
  JP2 = Header 2 [package=jst-2-smd]
  JP3 = Header 2 [package=jst-2-smd]  # not connected
  R24 = Resistor [tolerance=±5% resistance=22k package="0603 [SMD]"]
  R25 = Resistor [tolerance=±5% resistance=22k package="0603 [SMD]"]
  U10 = LM 358 Dual Op-Amp [package="DIP8 [THT]"]
  D10 = Diode [package=diode-1n4148]
  D11 = Diode [package=diode-1n4148]
  D12 = Zener Diode [part_number=1N4732A breakdown_voltage=3.6V package="300 mil [THT]"]
  R26 = Resistor [tolerance=±5% resistance=47k package="0603 [SMD]"]
  R27 = Resistor [tolerance=±5% resistance=330k package="0603 [SMD]"]
  R28 = Resistor [tolerance=±5% resistance=0 part_number=120k!! package="0603 [SMD]"]
  R29 = Resistor [tolerance=±5% resistance=1M part_number=ajustable package="0603 [SMD]"]
  R30 = Resistor [tolerance=±5% resistance=100k package=THT]
  C15 = Ceramic Capacitor [capacitance=0pF part_number=330nF package="100 mil [THT, multilayer]"]
  R31 = Resistor [tolerance=±5% resistance=1M package="0603 [SMD]"]

nets (from the schematic view):
  N1: U1.connector0, U1.connector1, R9.Pin_1, D3.cathode
  N2: U1.connector2, U1.connector6, R8.Pin_0
  5V: U1.connector3, U2.connector3, U3.connector7, U4.connector3, C8.+, U9.IN, U10.connector7, R27.Pin_0, R29.Pin_1
  N3: U1.connector4, R6.Pin_0, R7.Pin_0
  N4: U1.connector5, R5.Pin_0, R8.Pin_1
  GND: U1.connector7, RShunt.Pin_1, U2.connector7, U3.connector3, C3.1, R15.Pin_1, R4.Pin_0, R3.Pin_1, R7.Pin_1, U4.connector7, R22.Pin_1, U5.VSS, U7.VSS, C8.-, C9.-, C10.0, U10.connector3, R26.Pin_1, R28.Pin_1, C15.0, R31.Pin_0
  N5: RShunt.Pin_0, U2.connector4, R2.Pin_1, C12.-, C13.-, JP2.2
  N6: U2.connector0, R17.Pin_0, R30.Pin_1
  N7: U2.connector1, R17.Pin_1, R24.Pin_0
  N8: U2.connector2, R25.Pin_0, R28.Pin_0
  N9: U2.connector5, R14.Pin_1, R15.Pin_0
  N10: U2.connector6, D4.cathode
  N11: U3.connector0, R11.Pin_0, U4.connector1, U10.connector2
  N12: U3.connector1, R11.Pin_1, R10.Pin_0
  N13: U3.connector2, C3.0, R9.Pin_0, R26.Pin_0, R27.Pin_1
  N14: U3.connector4, R23.Pin_0
  N15: U3.connector5, U3.connector6, R10.Pin_1
  N16: R14.Pin_0, R25.Pin_1
  N17: R5.Pin_1, R4.Pin_1, R2.Pin_0
  N18: R3.Pin_0, R1.Pin_1, R6.Pin_1
  N19: R1.Pin_0, C12.+, L1.pin_1
  N20: U4.connector0, LED1.anode, D6.cathode
  N21: U4.connector2, U4.connector5, U4.connector6, U10.connector4
  N22: U4.connector4, R30.Pin_0, C15.1
  N23: R22.Pin_0, LED1.cathode
  VDD: U5.VDD, U7.VDD, C9.+, C10.1, U9.OUT
  N24: U5.VOUT, R23.Pin_1
  N25: U5.SCL, U7.SCL, D8.cathode
  N26: U5.SDA, U7.SDA, D9.cathode
  N27: U7.VOUT, R24.Pin_1
  N28: C13.+, L1.pin_0, JP2.1
  N29: U10.connector0, D10.A
  N30: U10.connector1, U10.connector5, D10.C, D11.C, D12.cathode
  N31: U10.connector6, D11.A
  N32: R29.Pin_0, R31.Pin_1

notes:
  Isense
  Vref
  Iref
  CC
  FBV
  FBI
  mVO
  mIO
  SCL
  SDA
  3.3v
  Output filter
  DC/DC output
  Out+
  Out-
  Feedback
  Vout=consign*94/10000 +0.72
  3L
  3R
  1L
  1R
  2L
  2R
  4L
  4R
  Variable
  5
